// Logisim project Regfile.circ as structural Verilog: 1 circuit, main circuit Register File
module Register_File (
  input  [1:0] Read_register_1,
  input  [1:0] Read_register_2,
  input  [1:0] write_register,
  input  [15:0] write_data,
  input  RegWrite,
  input  clock,
  output [15:0] Reg_0_Value,
  output [15:0] Reg_1_Value,
  output [15:0] Reg_2_Value,
  output [15:0] Reg_3_Value,
  output [15:0] Read_Data_1,
  output [15:0] Read_Data_2
);

  wire WReg0, WReg1, WReg2, WReg3;
  wire [15:0] controlled_buffer_1_out, controlled_buffer_2_out, controlled_buffer_3_out,
       controlled_buffer_4_out, WReg0Data, WReg1Data, WReg2Data, WReg3Data;

  Demultiplexer #(.select(2), .width(16)) demultiplexer_1 (
    .out0(WReg0Data), .out1(WReg1Data), .out2(WReg2Data), .out3(WReg3Data), .in(write_data),
    .sel(write_register), .en(clock));
  Demultiplexer #(.select(2)) demultiplexer_2 (
    .out0(WReg0), .out1(WReg1), .out2(WReg2), .out3(WReg3), .in(RegWrite), .sel(write_register), .en(clock));
  assign controlled_buffer_1_out = WReg0 ? WReg0Data : 16'bz;  // Controlled_Buffer controlled_buffer_1
  assign controlled_buffer_2_out = WReg1 ? WReg1Data : 16'bz;  // Controlled_Buffer controlled_buffer_2
  assign controlled_buffer_3_out = WReg2 ? WReg2Data : 16'bz;  // Controlled_Buffer controlled_buffer_3
  assign controlled_buffer_4_out = WReg3 ? WReg3Data : 16'bz;  // Controlled_Buffer controlled_buffer_4
  Register #(.width(16), .trigger("high")) r0 (
    .D(controlled_buffer_1_out), .Q(Reg_0_Value), .clk(clock));  // open: en, clr
  Register #(.width(16), .trigger("high")) r1 (
    .D(controlled_buffer_2_out), .Q(Reg_1_Value), .clk(clock));  // open: en, clr
  Register #(.width(16), .trigger("high")) r2 (
    .D(controlled_buffer_3_out), .Q(Reg_2_Value), .clk(clock));  // open: en, clr
  Register #(.width(16), .trigger("high")) r3 (
    .D(controlled_buffer_4_out), .Q(Reg_3_Value), .clk(clock));  // open: en, clr
  Multiplexer #(.select(2), .width(16), .enable("false")) multiplexer_1 (
    .in0(Reg_0_Value), .in1(Reg_1_Value), .in2(Reg_2_Value), .in3(Reg_3_Value), .out(Read_Data_1),
    .sel(Read_register_1));
  Multiplexer #(.select(2), .width(16), .enable("false")) multiplexer_2 (
    .in0(Reg_0_Value), .in1(Reg_1_Value), .in2(Reg_2_Value), .in3(Reg_3_Value), .out(Read_Data_2),
    .sel(Read_register_2));

  // Other names for the same wires on the sheet: clk = clock; RegRead1Select[1:0] = Read_register_1;
  //   RegRead2Select[1:0] = Read_register_2; RegWriteSelect[1:0] = write_register; RReg0[15:0] = Reg_0_Value;
  //   RReg1[15:0] = Reg_1_Value; RReg2[15:0] = Reg_2_Value; RReg3[15:0] = Reg_3_Value

  // Notes on the sheet:
  //   These are INPUTS to the circuit
  //   These are INPUTS to the circuit
  //   Yet again, the clock is not an actual clock, but an input, one that will be driven from a higher circuit
  //   DO NOT CHANGE THE LOCATIONS OF THE INPUTS/OUTPUTS! IF YOU DO SO, YOU NEED TO MAKE SURE THE PINS ARE AT THE RIGHT PLACE!
  //   These are OUTPUTS to the circuit
  //   These are OUTPUTS to the circuit
endmodule
