// Logisim project alu.circ as structural Verilog: 22 circuits, main circuit Arithmetic Logic Unit
module Arithmetic_Logic_Unit (
  input  [15:0] X,
  input  [15:0] Y,
  input  [3:0] Switch__S,
  output Signed_Overflow,
  output [15:0] RESULT,
  output Equal
);

  wire addOverflow, addp8Overflow, subOverflow, subp8Overflow;
  wire [15:0] addOut, addp8Out, andOut, orOut, sllvOut, sltOut, sravOut, srlvOut, subOut, subp8Out;

  equal equal_1 (.in_1(X), .in_2(Y), .out(Equal));
  add add_1 (.in_1(X), .in_2(Y), .result(addOut), .overflow(addOverflow));
  sub sub_1 (.in_1(X), .in_2(Y), .result(subOut), .overflow(subOverflow));
  sllv sllv_1 (.in_1(X), .in_2(Y), .out_3(sllvOut));
  srlv srlv_1 (.in_1(X), .in_2(Y), .out_3(srlvOut));
  srav srav_1 (.in_1(X), .in_2(Y), .out_3(sravOut));
  slt slt_1 (.in_1(X), .in_2(Y), .out(sltOut));
  \or  or_1 (.in_1(X), .in_2(Y), .out(orOut));
  \and  and_1 (.in_1(X), .in_2(Y), .out(andOut));
  addp8 addp8_1 (.x(X), .y(Y), .out(addp8Out), .overflow(addp8Overflow));
  subp8 subp8_1 (.x(X), .y(Y), .out(subp8Out), .overflow(subp8Overflow));
  Multiplexer #(.select(4), .width(16)) multiplexer_1 (
    .in0(addOut), .in1(subOut), .in2(sllvOut), .in3(srlvOut), .in4(sravOut), .in5(sltOut), .in6(orOut),
    .in7(andOut), .in8(addp8Out), .in9(subp8Out), .out(RESULT), .sel(Switch__S));  // open: in10, in11, in12, in13, in14, in15, en
  Multiplexer #(.select(2), .enable("false")) multiplexer_2 (
    .in0(addOverflow), .in1(subOverflow), .in2(addp8Overflow), .in3(subp8Overflow), .out(Signed_Overflow),
    .sel({Switch__S[3], Switch__S[0]}));

  // Other names for the same wires on the sheet: OutputSelect[3:0] = Switch__S;
  //   OverflowSelect[1:0] = {Switch__S[3], Switch__S[0]}; Overflow = Signed_Overflow

  // Notes on the sheet:
  //   INPUT to your circuit
  //   INPUTS to your circuit
  //   add
  //   sub
  //   sllv
  //   srlv
  //   srav
  //   DON'T CHANGE THE INPUTS AND OUTPUTS! IF YOU DO SO, YOU NEED TO MAKE SURE THE PINS ARE IN THE RIGHT PLACES!
  //   slt
  //   or
  //   and
  //   addp8
  //   subp8
  //   OUTPUTS of your circuit
endmodule

module add (
  input  [15:0] in_1,
  input  [15:0] in_2,
  output [15:0] result,
  output overflow
);

  wire ResultSignBit, XSignBit, YSignBit;

  BitSelector #(.width(16)) bitselector_1 (.in(in_1), .out(XSignBit), .sel(4'b1111));
  BitSelector #(.width(16)) bitselector_2 (.in(in_2), .out(YSignBit), .sel(4'b1111));
  Adder #(.width(16)) adder_1 (.a(in_1), .b(in_2), .out(result));  // open: cin, cout
  BitSelector #(.width(16)) bitselector_3 (.in(result), .out(ResultSignBit), .sel(4'b1111));
  AddOverflowCheck addoverflowcheck_1 (.x(XSignBit), .y(YSignBit), .result(ResultSignBit), .overflow(overflow));
endmodule

module sub (
  input  [15:0] in_1,
  input  [15:0] in_2,
  output [15:0] result,
  output overflow
);

  wire ResultSignBit, XSignBit, YSignBit;

  BitSelector #(.width(16)) bitselector_1 (.in(in_1), .out(XSignBit), .sel(4'b1111));
  BitSelector #(.width(16)) bitselector_2 (.in(in_2), .out(YSignBit), .sel(4'b1111));
  Subtractor #(.width(16)) subtractor_1 (.a(in_1), .b(in_2), .out(result));  // open: bin, bout
  BitSelector #(.width(16)) bitselector_3 (.in(result), .out(ResultSignBit), .sel(4'b1111));
  SubOverflowCheck suboverflowcheck_1 (.x(XSignBit), .y(YSignBit), .result(ResultSignBit), .overflow(overflow));
endmodule

module sllv (
  input  [15:0] in_1,
  input  [15:0] in_2,
  output [15:0] out_3
);

  wire [15:0] multiplexer_1_out, multiplexer_2_out, multiplexer_3_out, sll1_1_out, sll2_1_out, sll4_1_out,
       sll8_1_out;

  sll8 sll8_1 (.in_1(in_1), .out(sll8_1_out));
  Multiplexer #(.width(16)) multiplexer_1 (
    .in0(in_1), .in1(sll8_1_out), .out(multiplexer_1_out), .sel(in_2[3]));  // open: en
  sll4 sll4_1 (.in_1(multiplexer_1_out), .out(sll4_1_out));
  Multiplexer #(.width(16)) multiplexer_2 (
    .in0(multiplexer_1_out), .in1(sll4_1_out), .out(multiplexer_2_out), .sel(in_2[2]));  // open: en
  Multiplexer #(.width(16)) multiplexer_3 (
    .in0(multiplexer_2_out), .in1(sll2_1_out), .out(multiplexer_3_out), .sel(in_2[1]));  // open: en
  sll2 sll2_1 (.in_1(multiplexer_2_out), .out(sll2_1_out));
  sll1 sll1_1 (.in_1(multiplexer_3_out), .out(sll1_1_out));
  Multiplexer #(.width(16)) multiplexer_4 (
    .in0(multiplexer_3_out), .in1(sll1_1_out), .out(out_3), .sel(in_2[0]));  // open: en

  // Notes on the sheet:
  //   sll8
  //   sll4
  //   sll2
  //   sll1
endmodule

module srlv (
  input  [15:0] in_1,
  input  [15:0] in_2,
  output [15:0] out_3
);

  wire [15:0] multiplexer_1_out, multiplexer_2_out, multiplexer_3_out, sr1_1_out, sr2_1_out, sr4_1_out,
       sr8_1_out;

  sr8 sr8_1 (.in_1(in_1), .in_2(1'b0), .out(sr8_1_out));
  Multiplexer #(.width(16), .enable("false")) multiplexer_1 (
    .in0(in_1), .in1(sr8_1_out), .out(multiplexer_1_out), .sel(in_2[3]));
  sr4 sr4_1 (.in_1(multiplexer_1_out), .in_2(1'b0), .out(sr4_1_out));
  Multiplexer #(.width(16), .enable("false")) multiplexer_2 (
    .in0(multiplexer_1_out), .in1(sr4_1_out), .out(multiplexer_2_out), .sel(in_2[2]));
  sr2 sr2_1 (.in_1(multiplexer_2_out), .in_2(1'b0), .out(sr2_1_out));
  Multiplexer #(.width(16), .enable("false")) multiplexer_3 (
    .in0(multiplexer_2_out), .in1(sr2_1_out), .out(multiplexer_3_out), .sel(in_2[1]));
  sr1 sr1_1 (.in_1(multiplexer_3_out), .in_2(1'b0), .out(sr1_1_out));
  Multiplexer #(.width(16), .enable("false")) multiplexer_4 (
    .in0(multiplexer_3_out), .in1(sr1_1_out), .out(out_3), .sel(in_2[0]));

  // Notes on the sheet:
  //   sr8
  //   sr4
  //   sr2
  //   sr1
endmodule

module srav (
  input  [15:0] in_1,
  input  [15:0] in_2,
  output [15:0] out_3
);

  wire [15:0] multiplexer_1_out, multiplexer_2_out, multiplexer_3_out, sr1_1_out, sr2_1_out, sr4_1_out,
       sr8_1_out;

  sr8 sr8_1 (.in_1(in_1), .in_2(in_1[15]), .out(sr8_1_out));
  Multiplexer #(.width(16), .enable("false")) multiplexer_1 (
    .in0(in_1), .in1(sr8_1_out), .out(multiplexer_1_out), .sel(in_2[3]));
  sr4 sr4_1 (.in_1(multiplexer_1_out), .in_2(in_1[15]), .out(sr4_1_out));
  Multiplexer #(.width(16), .enable("false")) multiplexer_2 (
    .in0(multiplexer_1_out), .in1(sr4_1_out), .out(multiplexer_2_out), .sel(in_2[2]));
  sr2 sr2_1 (.in_1(multiplexer_2_out), .in_2(in_1[15]), .out(sr2_1_out));
  Multiplexer #(.width(16), .enable("false")) multiplexer_3 (
    .in0(multiplexer_2_out), .in1(sr2_1_out), .out(multiplexer_3_out), .sel(in_2[1]));
  sr1 sr1_1 (.in_1(multiplexer_3_out), .in_2(in_1[15]), .out(sr1_1_out));
  Multiplexer #(.width(16), .enable("false")) multiplexer_4 (
    .in0(multiplexer_3_out), .in1(sr1_1_out), .out(out_3), .sel(in_2[0]));

  // Notes on the sheet:
  //   sr8
  //   sr4
  //   sr2
  //   sr1
endmodule

module slt (
  input  [15:0] in_1,
  input  [15:0] in_2,
  output [15:0] out
);

  Comparator #(.width(16)) comparator_1 (.a(in_1), .b(in_2), .lt(out[0]));  // open: gt, eq

  assign out[15:1] = {15{1'b0}};
endmodule

module \or  (
  input  [15:0] in_1,
  input  [15:0] in_2,
  output [15:0] out
);

  assign out = in_1 | in_2;  // OR_Gate or_1, 16 bits wide
endmodule

module \and  (
  input  [15:0] in_1,
  input  [15:0] in_2,
  output [15:0] out
);

  assign out = in_1 & in_2;  // AND_Gate and_1, 16 bits wide
endmodule

module addp8 (
  input  [15:0] x,
  input  [15:0] y,
  output [15:0] out,
  output overflow
);

  wire addoverflowcheck_1_overflow, addoverflowcheck_2_overflow, ResultHiSignBit, ResultLoSignBit,
       XHiSignBit, XLoSignBit, YHiSignBit, YLoSignBit;

  BitSelector bitselector_1 (.in(x[15:8]), .out(XHiSignBit), .sel(3'b111));
  BitSelector bitselector_2 (.in(y[15:8]), .out(YHiSignBit), .sel(3'b111));
  BitSelector bitselector_3 (.in(x[7:0]), .out(XLoSignBit), .sel(3'b111));
  BitSelector bitselector_4 (.in(y[7:0]), .out(YLoSignBit), .sel(3'b111));
  Adder adder_1 (.a(x[15:8]), .b(y[15:8]), .out(out[15:8]));  // open: cin, cout
  Adder adder_2 (.a(x[7:0]), .b(y[7:0]), .out(out[7:0]));  // open: cin, cout
  AddOverflowCheck addoverflowcheck_1 (
    .x(XHiSignBit), .y(YHiSignBit), .result(ResultHiSignBit), .overflow(addoverflowcheck_1_overflow));
  AddOverflowCheck addoverflowcheck_2 (
    .x(XHiSignBit), .y(YHiSignBit), .result(ResultHiSignBit), .overflow(addoverflowcheck_2_overflow));
  BitSelector bitselector_5 (.in(out[15:8]), .out(ResultHiSignBit), .sel(3'b111));
  BitSelector bitselector_6 (.in(out[7:0]), .out(ResultLoSignBit), .sel(3'b111));
  or or_1 (overflow, addoverflowcheck_1_overflow, addoverflowcheck_2_overflow);
endmodule

module subp8 (
  input  [15:0] x,
  input  [15:0] y,
  output [15:0] out,
  output overflow
);

  wire ResultHiSignBit, ResultLoSignBit, suboverflowcheck_1_overflow, suboverflowcheck_2_overflow,
       XHiSignBit, XLoSignBit, YHiSignBit, YLoSignBit;

  BitSelector bitselector_1 (.in(x[15:8]), .out(XHiSignBit), .sel(3'b111));
  BitSelector bitselector_2 (.in(y[15:8]), .out(YHiSignBit), .sel(3'b111));
  BitSelector bitselector_3 (.in(x[7:0]), .out(XLoSignBit), .sel(3'b111));
  BitSelector bitselector_4 (.in(y[7:0]), .out(YLoSignBit), .sel(3'b111));
  Subtractor subtractor_1 (.a(x[15:8]), .b(y[15:8]), .out(out[15:8]));  // open: bin, bout
  Subtractor subtractor_2 (.a(x[7:0]), .b(y[7:0]), .out(out[7:0]));  // open: bin, bout
  SubOverflowCheck suboverflowcheck_1 (
    .x(XHiSignBit), .y(YHiSignBit), .result(ResultHiSignBit), .overflow(suboverflowcheck_1_overflow));
  SubOverflowCheck suboverflowcheck_2 (
    .x(XHiSignBit), .y(YHiSignBit), .result(ResultHiSignBit), .overflow(suboverflowcheck_2_overflow));
  BitSelector bitselector_5 (.in(out[15:8]), .out(ResultHiSignBit), .sel(3'b111));
  BitSelector bitselector_6 (.in(out[7:0]), .out(ResultLoSignBit), .sel(3'b111));
  or or_1 (overflow, suboverflowcheck_1_overflow, suboverflowcheck_2_overflow);
endmodule

module equal (
  input  [15:0] in_1,
  input  [15:0] in_2,
  output out
);

  Comparator #(.width(16)) comparator_1 (.a(in_1), .b(in_2), .eq(out));  // open: gt, lt
endmodule

module sll8 (
  input  [15:0] in_1,
  output [15:0] out
);


  assign out = {in_1[7:0], {8{1'b0}}};
endmodule

module sll4 (
  input  [15:0] in_1,
  output [15:0] out
);


  assign out = {in_1[11:0], 4'b0000};
endmodule

module sll2 (
  input  [15:0] in_1,
  output [15:0] out
);


  assign out = {in_1[13:0], 2'b00};
endmodule

module sll1 (
  input  [15:0] in_1,
  output [15:0] out
);


  assign out = {in_1[14:0], 1'b0};
endmodule

module sr8 (
  input  [15:0] in_1,
  input  in_2,
  output [15:0] out
);

  Multiplexer #(.width(8)) multiplexer_1 (.in0({8{1'b0}}), .in1({8{1'b1}}), .out(out[15:8]), .sel(in_2));  // open: en

  assign out[7:0] = in_1[15:8];
endmodule

module sr4 (
  input  [15:0] in_1,
  input  in_2,
  output [15:0] out
);

  Multiplexer #(.width(4)) multiplexer_1 (.in0(4'b0000), .in1(4'b1111), .out(out[15:12]), .sel(in_2));  // open: en

  assign out[11:0] = in_1[15:4];
endmodule

module sr2 (
  input  [15:0] in_1,
  input  in_2,
  output [15:0] out
);

  Multiplexer #(.width(2)) multiplexer_1 (.in0(2'b00), .in1(2'b11), .out(out[15:14]), .sel(in_2));  // open: en

  assign out[13:0] = in_1[15:2];
endmodule

module sr1 (
  input  [15:0] in_1,
  input  in_2,
  output [15:0] out
);

  Multiplexer multiplexer_1 (.in0(1'b0), .in1(1'b1), .out(out[15]), .sel(in_2));  // open: en

  assign out[14:0] = in_1[15:1];
endmodule

module AddOverflowCheck (
  input  x,
  input  y,
  input  result,
  output overflow
);

  wire and_1_out, and_2_out, not_1_out, not_2_out, not_3_out;

  not not_1 (not_1_out, x);
  not not_2 (not_2_out, y);
  not not_3 (not_3_out, result);
  and and_1 (and_1_out, not_1_out, not_2_out, result);
  or or_1 (overflow, and_1_out, and_2_out);
  and and_2 (and_2_out, x, y, not_3_out);
endmodule

module SubOverflowCheck (
  input  x,
  input  y,
  input  result,
  output overflow
);

  wire and_1_out, and_2_out, not_1_out, not_2_out, not_3_out;

  not not_1 (not_1_out, x);
  not not_2 (not_2_out, y);
  not not_3 (not_3_out, result);
  and and_1 (and_1_out, not_1_out, y, result);
  and and_2 (and_2_out, x, not_2_out, not_3_out);
  or or_1 (overflow, and_1_out, and_2_out);
endmodule
