// Logisim project cpu.circ as structural Verilog: 24 circuits, main circuit main
// CPU
module main (
  input  [15:0] From_Instr_Mem,
  input  clk,
  output [15:0] r0,
  output [15:0] r1,
  output [15:0] r2,
  output [15:0] r3,
  output [15:0] Display_0,
  output [15:0] Display_1,
  output [15:0] To_Instr_Mem,
  output [15:0] Data_Mem_Data,
  output [15:0] Data_Mem_Addr,
  output Data_Mem_Write
);

  wire ALUsrc, and_1_out, bitselector_1_out, branch_jump, demultiplexer_1_out0, demultiplexer_1_out1, disp,
       Equal, ExtOp, instruction_decoder_1_regdest, instruction_decoder_1_regwrite, isjr, islui, LinkAddr,
       MemRead, nbranch, not_1_out, not_2_out, Overflow, register_file_1_p1;
  wire [1:0] instruction_decoder_1_out_8, instruction_decoder_1_out_9, instruction_decoder_1_out_12,
       multiplexer_3_out, multiplexer_4_out, PC_select;
  wire [3:0] funct;
  wire [7:0] instruction_decoder_1_imm_offset;
  wire [15:0] adder_1_out, controlled_buffer_3_out, data_memory_1_dataout, Instr,
       instruction_decoder_1_jumpaddr, JumpAddr, luiswitch_1_address, luiswitch_1_data_in, multiplexer_2_out,
       multiplexer_5_out, multiplexer_6_out, npc_sel_1_newpc, Offset, register_1_q, register_2_q,
       register_file_1_p13, rs, WriteData;

  Register #(.width(16)) register_1 (.D(npc_sel_1_newpc), .Q(register_1_q), .clk(clk));  // open: en, clr
  nPC_sel npc_sel_1 (
    .CurrInstr(register_1_q), .Immediate(Offset), .JumpAddr(JumpAddr), .NewPC(npc_sel_1_newpc),
    .in_4(PC_select));
  Register #(.width(16)) register_2 (.D(register_1_q), .Q(register_2_q), .clk(clk));  // open: en, clr
  Comparator #(.width(2), .mode("unsigned")) comparator_1 (.a(PC_select), .b(2'b00), .gt(branch_jump));  // open: eq, lt
  Multiplexer #(.width(16), .enable("false")) multiplexer_1 (
    .in0(register_1_q), .in1(register_2_q), .out(To_Instr_Mem), .sel(branch_jump));
  assign JumpAddr = isjr ? rs : 16'bz;  // Controlled_Buffer controlled_buffer_1
  // Probe on multiplexer_2_out
  Multiplexer #(.width(16), .enable("false")) multiplexer_2 (
    .in0(From_Instr_Mem), .in1(16'h6), .out(multiplexer_2_out), .sel(branch_jump));
  // Probe on Instr
  Register #(.width(16)) register_3 (.D(multiplexer_2_out), .Q(Instr), .clk(clk));  // open: en, clr
  Instruction_Decoder instruction_decoder_1 (
    .Instruction_In(Instr), .RegDest(instruction_decoder_1_regdest), .out_8(instruction_decoder_1_out_8),
    .out_9(instruction_decoder_1_out_9), .out_12(instruction_decoder_1_out_12),
    .RegWrite(instruction_decoder_1_regwrite), .SignExtend(ExtOp), .funct(funct),
    .imm_offset(instruction_decoder_1_imm_offset), .ALUsrc(ALUsrc), .MemWrite(Data_Mem_Write), .islui(islui),
    .MemRead(MemRead), .PCSelect(PC_select), .Equal(Equal), .nbranch(nbranch), .CurrentPC(To_Instr_Mem),
    .isjr(isjr), .disp(disp), .jumpaddr(instruction_decoder_1_jumpaddr), .LinkAddr(LinkAddr));
  Multiplexer #(.width(2), .enable("false")) multiplexer_3 (
    .in0(instruction_decoder_1_out_12), .in1(2'b11), .out(multiplexer_3_out), .sel(LinkAddr));
  assign JumpAddr = not_1_out ? instruction_decoder_1_jumpaddr : 16'bz;  // Controlled_Buffer controlled_buffer_2
  not not_1 (not_1_out, isjr);
  Multiplexer #(.width(2), .enable("false")) multiplexer_4 (
    .in0(instruction_decoder_1_out_9), .in1(multiplexer_3_out), .out(multiplexer_4_out),
    .sel(instruction_decoder_1_regdest));
  ext ext_1 (.in_1(ExtOp), .in_2(instruction_decoder_1_imm_offset), .Result(Offset));
  // Register_File register_file_1: pin names not known; wires that end beside it: register_file_1_p1, multiplexer_4_out, multiplexer_3_out, instruction_decoder_1_out_8, WriteData, instruction_decoder_1_regwrite, r0, r1, clk, r2, r3, rs, register_file_1_p13, register_file_1_p1
  Multiplexer #(.width(16), .enable("false")) multiplexer_5 (
    .in0(rs), .in1(16'h8), .out(multiplexer_5_out), .sel(islui));
  Multiplexer #(.width(16), .enable("false")) multiplexer_6 (
    .in0(register_file_1_p13), .in1(Offset), .out(multiplexer_6_out), .sel(and_1_out));
  and and_1 (and_1_out, ALUsrc, nbranch);
  luiswitch luiswitch_1 (
    ._8(multiplexer_5_out), .imm(multiplexer_6_out), .Data_In(luiswitch_1_data_in),
    .Address(luiswitch_1_address), .in_3(islui));
  assign controlled_buffer_3_out = LinkAddr ? adder_1_out : 16'bz;  // Controlled_Buffer controlled_buffer_3
  // Arithmetic_Logic_Unit arithmetic_logic_unit_1: pin names not known; wires that end beside it: luiswitch_1_data_in, luiswitch_1_address, Equal, Overflow, funct, controlled_buffer_3_out
  Adder #(.width(16)) adder_1 (.a(To_Instr_Mem), .b(16'h1), .out(adder_1_out));  // open: cin, cout
  Multiplexer #(.width(16), .enable("false")) multiplexer_7 (
    .in0(data_memory_1_dataout), .in1(Data_Mem_Data), .out(WriteData), .sel(not_2_out));
  not not_2 (not_2_out, MemRead);
  Address_Data_Select address_data_select_1 (
    .ALUresult(controlled_buffer_3_out), .Address(register_file_1_p13), .Data_In(Data_Mem_Data),
    .Address_2(Data_Mem_Addr), .MemWrite(Data_Mem_Write), .MemRead(MemRead));
  Data_Memory data_memory_1 (
    .DataIn(Data_Mem_Data), .Address(Data_Mem_Addr), .DataOut(data_memory_1_dataout),
    .MemWrite(Data_Mem_Write), .clk(clk));  // open: Reset
  LED led_1 (.in(Overflow));
  Demultiplexer #(.enable("false")) demultiplexer_1 (
    .out0(demultiplexer_1_out0), .out1(demultiplexer_1_out1), .in(disp), .sel(bitselector_1_out));
  Hex_Digit_Display hex_digit_display_1 (.value(Display_0[11:8]));  // open: dp
  Hex_Digit_Display hex_digit_display_2 (.value(Display_0[15:12]));  // open: dp
  BitSelector #(.width(16)) bitselector_1 (.in(Offset), .out(bitselector_1_out), .sel(4'b0000));
  Hex_Digit_Display hex_digit_display_3 (.value(Display_0[7:4]));  // open: dp
  Hex_Digit_Display hex_digit_display_4 (.value(Display_0[3:0]));  // open: dp
  Register #(.width(16)) register_4 (.D(rs), .en(demultiplexer_1_out0), .Q(Display_0), .clk(clk));  // open: clr
  Hex_Digit_Display hex_digit_display_5 (.value(Display_1[15:12]));  // open: dp
  Hex_Digit_Display hex_digit_display_6 (.value(Display_1[11:8]));  // open: dp
  Hex_Digit_Display hex_digit_display_7 (.value(Display_1[7:4]));  // open: dp
  Register #(.width(16)) register_5 (.D(rs), .en(demultiplexer_1_out1), .Q(Display_1), .clk(clk));  // open: clr
  Hex_Digit_Display hex_digit_display_8 (.value(Display_1[3:0]));  // open: dp

  // Other names for the same wires on the sheet: Address[15:0] = Data_Mem_Addr; CurrPC[15:0] = To_Instr_Mem;
  //   d0[15:0] = Display_0; d1[15:0] = Display_1; Data[15:0] = Data_Mem_Data; MemWrite = Data_Mem_Write

  // Notes on the sheet:
  //   This is the current PC that you need to send as OUTPUT
  //   This is the instruction that you would receive as INPUT
  //   This is a CLK that is an INPUT driven from the harness.
  //   Remember, this circuit is loaded from the harness to be tested!
  //   DO NOT CHANGE THE LOCATIONS OF THE INPUTS OR OUTPUTS! IF YOU DO SO, YOU NEED TO MAKE SURE THE PINS ARE IN THE RIGHT PLACES!
  //   These are OUTPUTS of the circuit
  //   rd
  //   rt
  //   rs
  //   RegDest
  //   RegWrite
  //   imm
  //   R[rt]
  //   R[rs]
  //   imm
  //   These are OUTPUTS of the circuit
endmodule

module Data_Memory (
  input  [15:0] DataIn,
  input  [15:0] Address,
  input  clk,
  input  Reset,
  input  MemWrite,
  output [15:0] DataOut
);

  wire not_1_out;

  assign DataOut = MemWrite ? DataIn : 16'bz;  // Controlled_Buffer controlled_buffer_1
  RAM #(.addrWidth(16), .dataWidth(16)) ram_1 (
    .addr(Address), .data(DataOut), .sel(1'b1), .clk(clk), .ld(not_1_out), .clr(Reset));
  not not_1 (not_1_out, MemWrite);
endmodule

module Instruction_Decoder (
  input  [15:0] CurrentPC,
  input  [15:0] Instruction_In,
  input  Equal,
  output [3:0] funct,
  output SignExtend,
  output MemRead,
  output RegDest,
  output [1:0] out_8,
  output [1:0] out_9,
  output nbranch,
  output ALUsrc,
  output [1:0] out_12,
  output RegWrite,
  output [7:0] imm_offset,
  output isjr,
  output MemWrite,
  output islui,
  output disp,
  output [1:0] PCSelect,
  output [15:0] jumpaddr,
  output LinkAddr
);

  wire disp_t, I_MemRead, I_MemWrite, I_nbranch, I_RegDest, I_RegWrite, I_SignExt, islui_t, J_Imm_Addr,
       J_RegDest, J_RegWrite, J_SignExt, linkaddr_t, R_Imm_Addr, R_RegDest, R_RegWrite, R_SignExt;
  wire [1:0] I_PCSel, I_rd, I_rs, I_rt, J_PCSel, J_rd, J_rs, J_rt, opcode, R_rd, R_rs, R_rt;
  wire [5:0] I_funct, R_funct;
  wire [5:4] funct_t;
  wire [7:0] I_Imm;
  wire [15:0] jumpaddr_t;

  Multiplexer #(.select(2), .enable("false")) multiplexer_1 (
    .in0(1'b0), .in1(1'b0), .in2(I_MemRead), .in3(1'b0), .out(MemRead), .sel(opcode));
  Multiplexer #(.select(2), .enable("false")) multiplexer_2 (
    .in0(1'b0), .in1(linkaddr_t), .in2(1'b0), .in3(1'b0), .out(LinkAddr), .sel(opcode));
  R_type_Instruction_Decode r_type_instruction_decode_1 (
    .in_1(Instruction_In), .rd(R_rd), .rt(R_rt), .rs(R_rs), .RegWrite(R_RegWrite), .RegDest(R_RegDest),
    .Imm_Addr(R_Imm_Addr), .Signed(R_SignExt), .funct(R_funct));
  J_type_Instruction_Decoder j_type_instruction_decoder_1 (
    .in_2(Instruction_In), .rt(J_rt), .rs(J_rs), .RegDest(J_RegDest), .Imm_Addr(J_Imm_Addr),
    .Signed(J_SignExt), .PCSelect(J_PCSel), .CurrentPC(CurrentPC), .jumpaddr(jumpaddr_t),
    .RegWrite(J_RegWrite), .rd(J_rd), .LinkAddr(linkaddr_t), .isjr(isjr));
  Multiplexer #(.select(2), .enable("false")) multiplexer_3 (
    .in0(1'b0), .in1(1'b0), .in2(disp_t), .out(disp), .sel(opcode));  // open: in3
  Type_Decoder type_decoder_1 (.in_1(Instruction_In), .Type(opcode));
  Multiplexer #(.select(2), .width(8), .enable("false")) multiplexer_4 (
    .in0({8{1'b1}}), .in1({8{1'b1}}), .in2(I_Imm), .in3({8{1'b1}}), .out(imm_offset), .sel(opcode));
  Multiplexer #(.select(2), .width(16), .enable("false")) multiplexer_5 (
    .in0({16{1'b0}}), .in1(jumpaddr_t), .in2({16{1'b0}}), .in3({16{1'b0}}), .out(jumpaddr), .sel(opcode));
  I_type_Instruction_Decoder i_type_instruction_decoder_1 (
    .in_2(Instruction_In), .rd(I_rd), .rt(I_rt), .rs(I_rs), .SignOrUnsign(I_SignExt), .RegWrite(I_RegWrite),
    .RegDest(I_RegDest), .funct(I_funct), .Imm_Offset(I_Imm), .MemWrite(I_MemWrite), .islui(islui_t),
    .MemRead(I_MemRead), .Equal(Equal), .PCSel(I_PCSel), .nbranch(I_nbranch), .display(disp_t));
  Multiplexer #(.select(2), .enable("false")) multiplexer_6 (
    .in0(1'b0), .in1(1'b0), .in2(I_MemWrite), .in3(1'b0), .out(MemWrite), .sel(opcode));
  Multiplexer #(.select(2), .enable("false")) multiplexer_7 (
    .in0(1'b0), .in1(1'b0), .in2(islui_t), .in3(1'b0), .out(islui), .sel(opcode));
  Multiplexer #(.select(2), .enable("false")) multiplexer_8 (
    .in0(1'b1), .in1(1'b1), .in2(I_nbranch), .in3(1'b1), .out(nbranch), .sel(opcode));
  Multiplexer #(.select(2), .width(2), .enable("false")) multiplexer_9 (
    .in0(2'b00), .in1(J_PCSel), .in2(I_PCSel), .in3(2'b00), .out(PCSelect), .sel(opcode));
  Multiplexer #(.select(2), .width(2), .enable("false")) multiplexer_10 (
    .in0(R_rs), .in1(J_rs), .in2(I_rs), .out(out_8), .sel(opcode));  // open: in3
  Multiplexer #(.select(2), .width(2), .enable("false")) multiplexer_11 (
    .in0(R_rd), .in1(J_rd), .in2(I_rd), .out(out_9), .sel(opcode));  // open: in3
  Multiplexer #(.select(2), .width(2), .enable("false")) multiplexer_12 (
    .in0(R_rt), .in1(J_rt), .in2(I_rt), .out(out_12), .sel(opcode));  // open: in3
  Multiplexer #(.select(2), .width(6), .enable("false")) multiplexer_13 (
    .in0(R_funct), .in1({6{1'b1}}), .in2(I_funct), .out({funct_t, funct}), .sel(opcode));  // open: in3
  ALUsrcSel alusrcsel_1 (.in_1(opcode), .Sign(ALUsrc));
  Multiplexer #(.select(2), .enable("false")) multiplexer_14 (
    .in0(R_RegDest), .in1(J_RegDest), .in2(I_RegDest), .out(RegDest), .sel(opcode));  // open: in3
  Multiplexer #(.select(2), .enable("false")) multiplexer_15 (
    .in0(R_RegWrite), .in1(J_RegWrite), .in2(I_RegWrite), .out(RegWrite), .sel(opcode));  // open: in3
  Multiplexer #(.select(2), .enable("false")) multiplexer_16 (
    .in0(R_SignExt), .in1(J_SignExt), .in2(I_SignExt), .out(SignExtend), .sel(opcode));  // open: in3

  // Other names for the same wires on the sheet: CurrPC[15:0] = CurrentPC; funct_t[3:0] = funct; rd[1:0] = out_9;
  //   rs[1:0] = out_8; rt[1:0] = out_12

  // Notes on the sheet:
  //   0: write to rd
  //   1: write to rt
endmodule

// R-type decoder
module R_type_Instruction_Decode (
  input  [15:0] in_1,
  output [5:0] funct,
  output [1:0] rd,
  output [1:0] rt,
  output [1:0] rs,
  output RegWrite,
  output RegDest,
  output Imm_Addr,
  output Signed
);

  BitSelector #(.width(16), .group(2)) bitselector_1 (.in(in_1), .out(rd), .sel(3'b011));
  BitSelector #(.width(16), .group(2)) bitselector_2 (.in(in_1), .out(rt), .sel(3'b100));
  BitSelector #(.width(16), .group(2)) bitselector_3 (.in(in_1), .out(rs), .sel(3'b101));
  BitSelector #(.width(16), .group(6)) bitselector_4 (.in(in_1), .out(funct), .sel(2'b00));

  assign Imm_Addr = 1'b0;
  assign RegDest = 1'b0;
  assign RegWrite = 1'b1;
  assign Signed = 1'b0;

  // Notes on the sheet:
  //   (enable write to register)
  //   (select rd as destination register)
endmodule

// I-type decoder
module I_type_Instruction_Decoder (
  input  Equal,
  input  [15:0] in_2,
  output [1:0] rd,
  output [1:0] rt,
  output [1:0] rs,
  output [7:0] Imm_Offset,
  output MemRead,
  output RegDest,
  output islui,
  output MemWrite,
  output display,
  output nbranch,
  output [1:0] PCSel,
  output RegWrite,
  output [5:0] funct,
  output SignOrUnsign
);

  wire addiRW, addiSOU, andiRW, andiSOU, beqRW, beqSOU, bneRW, bneSOU, dispRW, dispSOU, lui, luiRW, luiSOU,
       lwRW, lwSOU, MemRead_t, MemWrite_t, multiplexer_8_out, oriRW, oriSOU, swRW, swSOU;
  wire [1:0] beqPCSel, bnePCSel;
  wire [3:0] InstrSelect;
  wire [5:0] addifunct, andifunct, luifunct, lwfunct, orifunct, swfunct;

  beq beq_1 (.Equal(Equal), .Sign(beqSOU), .RegWrite(beqRW), .PCSel(beqPCSel));  // open: nbranch
  ori ori_1 (.Sign(oriSOU), .RegWrite(oriRW), .funct(orifunct));
  lui lui_1 (.Sign(luiSOU), .RegWrite(luiRW), .funct(luifunct), .islui(lui));
  Multiplexer #(.select(4)) multiplexer_1 (
    .in0(1'b0), .in1(1'b0), .in2(1'b0), .in3(1'b0), .in4(1'b0), .in5(1'b0), .in6(1'b0), .in7(1'b0),
    .in8(1'b0), .in9(1'b0), .in10(1'b0), .in11(1'b0), .in12(1'b1), .in13(1'b0), .in14(1'b0), .in15(1'b0),
    .out(display), .sel(InstrSelect));  // open: en
  Multiplexer #(.select(4), .width(6), .disabled(0), .enable("false")) multiplexer_2 (
    .in0({6{1'b1}}), .in1({6{1'b1}}), .in2({6{1'b1}}), .in3({6{1'b1}}), .in4({6{1'b1}}), .in5(addifunct),
    .in6(andifunct), .in7(orifunct), .in8({6{1'b1}}), .in9(swfunct), .in10(luifunct), .in11(lwfunct),
    .in12({6{1'b1}}), .in13({6{1'b1}}), .in14({6{1'b1}}), .in15({6{1'b1}}), .out(funct), .sel(InstrSelect));
  BitSelector #(.width(16), .group(4)) bitselector_1 (.in(in_2), .out(InstrSelect), .sel(2'b11));
  BitSelector #(.width(16), .group(2)) bitselector_2 (.in(in_2), .out(rt), .sel(3'b100));
  BitSelector #(.width(16), .group(8)) bitselector_3 (.in(in_2), .out(Imm_Offset), .sel(1'b0));
  addi addi_1 (.Sign(addiSOU), .RegWrite(addiRW), .funct(addifunct));
  bne bne_1 (.Equal(Equal), .Sign(bneSOU), .RegWrite(bneRW), .PCSel(bnePCSel));  // open: nbranch
  lw lw_1 (.Sign(lwSOU), .RegWrite(lwRW), .funct(lwfunct), .MemRead(MemRead_t));
  BitSelector #(.width(16), .group(2)) bitselector_4 (.in(in_2), .out(rs), .sel(3'b101));
  sw sw_1 (.Sign(swSOU), .RegWrite(swRW), .funct(swfunct), .MemWrite(MemWrite_t));
  Multiplexer #(.select(4), .disabled(0), .enable("false")) multiplexer_3 (
    .in0(1'b0), .in1(1'b0), .in2(1'b0), .in3(1'b0), .in4(beqSOU), .in5(addiSOU), .in6(andiSOU), .in7(oriSOU),
    .in8(bneSOU), .in9(swSOU), .in10(luiSOU), .in11(lwSOU), .in12(dispSOU), .in13(1'b0), .in14(1'b0),
    .in15(1'b0), .out(SignOrUnsign), .sel(InstrSelect));
  andi andi_1 (.Sign(andiSOU), .RegWrite(andiRW), .funct(andifunct));
  disp disp_1 (.Sign(dispSOU), .RegWrite(dispRW));
  Multiplexer #(.select(4)) multiplexer_4 (
    .in0(1'b0), .in1(1'b0), .in2(1'b0), .in3(1'b0), .in4(1'b0), .in5(1'b0), .in6(1'b0), .in7(1'b0),
    .in8(1'b0), .in9(MemWrite_t), .in10(1'b0), .in11(1'b0), .in12(1'b0), .in13(1'b0), .in14(1'b0),
    .in15(1'b0), .out(MemWrite), .sel(InstrSelect));  // open: en
  Multiplexer #(.select(4)) multiplexer_5 (
    .in0(1'b0), .in1(1'b0), .in2(1'b0), .in3(1'b0), .in4(1'b0), .in5(1'b0), .in6(1'b0), .in7(1'b0),
    .in8(1'b0), .in9(1'b0), .in10(lui), .in11(1'b0), .in12(1'b0), .in13(1'b0), .in14(1'b0), .in15(1'b0),
    .out(islui), .sel(InstrSelect));  // open: en
  Multiplexer #(.select(4), .width(2)) multiplexer_6 (
    .in0(2'b00), .in1(2'b00), .in2(2'b00), .in3(2'b00), .in4(beqPCSel), .in5(2'b00), .in6(2'b00),
    .in7(2'b00), .in8(bnePCSel), .in9(2'b00), .in10(2'b00), .in11(2'b00), .in12(2'b00), .in13(2'b00),
    .in14(2'b00), .in15(2'b00), .out(PCSel), .sel(InstrSelect));  // open: en
  Multiplexer #(.select(4)) multiplexer_7 (
    .in0(1'b0), .in1(1'b0), .in2(1'b0), .in3(1'b0), .in4(1'b0), .in5(1'b0), .in6(1'b0), .in7(1'b0),
    .in8(1'b0), .in9(1'b0), .in10(1'b0), .in11(MemRead_t), .in12(1'b0), .in13(1'b0), .in14(1'b0),
    .in15(1'b0), .out(MemRead), .sel(InstrSelect));  // open: en
  not not_1 (nbranch, multiplexer_8_out);
  Multiplexer #(.select(4)) multiplexer_8 (
    .in0(1'b0), .in1(1'b0), .in2(1'b0), .in3(1'b0), .in4(1'b1), .in5(1'b0), .in6(1'b0), .in7(1'b0),
    .in8(1'b1), .in9(1'b0), .in10(1'b0), .in11(1'b0), .in12(1'b0), .in13(1'b0), .in14(1'b0), .in15(1'b0),
    .out(multiplexer_8_out), .sel(InstrSelect));  // open: en
  Multiplexer #(.select(4), .enable("false")) multiplexer_9 (
    .in0(1'b0), .in1(1'b0), .in2(1'b0), .in3(1'b0), .in4(beqRW), .in5(addiRW), .in6(andiRW), .in7(oriRW),
    .in8(bneRW), .in9(swRW), .in10(luiRW), .in11(lwRW), .in12(dispRW), .in13(1'b0), .in14(1'b0), .in15(1'b0),
    .out(RegWrite), .sel(InstrSelect));

  assign rd = 2'b11;
  assign RegDest = 1'b1;

  // Notes on the sheet:
  //   (rd is not used)
  //   (select rt as destination register)
endmodule

// J-type decoder
module J_type_Instruction_Decoder (
  input  [15:0] CurrentPC,
  input  [15:0] in_2,
  output isjr,
  output LinkAddr,
  output [1:0] rt,
  output [1:0] rs,
  output [1:0] rd,
  output RegDest,
  output Imm_Addr,
  output Signed,
  output [1:0] PCSelect,
  output [15:0] jumpaddr,
  output RegWrite
);

  wire [15:0] jaljumpaddr, jjumpaddr;

  Multiplexer #(.select(2), .enable("false")) multiplexer_1 (
    .in0(1'b0), .in1(1'b0), .in2(1'b0), .in3(1'b1), .out(isjr), .sel(in_2[13:12]));
  jal jal_1 (.CurrentPC(CurrentPC), .Target_addr(in_2), .jumpaddr(jaljumpaddr), .PCSel(PCSelect));
  j j_1 (.CurrentPC(CurrentPC), .Target_Addr(in_2), .jumpaddr(jjumpaddr), .PCSel(PCSelect));
  jr jr_1 (.in_1(in_2), .rs(rs));
  Multiplexer #(.select(2), .width(16), .enable("false")) multiplexer_2 (
    .in0({16{1'b0}}), .in1(jaljumpaddr), .in2(jjumpaddr), .in3({16{1'b0}}), .out(jumpaddr), .sel(in_2[13:12]));
  Multiplexer #(.select(2), .enable("false")) multiplexer_3 (
    .in0(1'b0), .in1(1'b1), .in2(1'b0), .in3(1'b0), .out(RegWrite), .sel(in_2[13:12]));
  Multiplexer #(.select(2), .width(2), .enable("false")) multiplexer_4 (
    .in0(2'b00), .in1(2'b11), .in2(2'b00), .in3(2'b00), .out(rd), .sel(in_2[13:12]));
  Multiplexer #(.select(2), .enable("false")) multiplexer_5 (
    .in0(1'b0), .in1(1'b1), .in2(1'b0), .in3(1'b0), .out(LinkAddr), .sel(in_2[13:12]));

  assign Imm_Addr = 1'b0;
  assign RegDest = 1'b0;
  assign rt = 2'b00;
  assign Signed = 1'b0;

  // Other names for the same wires on the sheet: CurrPC[15:0] = CurrentPC; Instruction_In[15:0] = in_2;
  //   OpSelect[1:0] = in_2[13:12]; PCSel[1:0] = PCSelect
endmodule

module beq (
  input  Equal,
  output nbranch,
  output Sign,
  output RegWrite,
  output [1:0] PCSel
);

  Multiplexer #(.width(2), .enable("false")) multiplexer_1 (.in0(2'b00), .in1(2'b01), .out(PCSel), .sel(Equal));

  assign nbranch = 1'b0;
  assign RegWrite = 1'b0;
  assign Sign = 1'b1;
endmodule

module addi (
  output Sign,
  output RegWrite,
  output [5:0] funct
);


  assign funct = {6{1'b0}};
  assign RegWrite = 1'b1;
  assign Sign = 1'b1;
endmodule

module andi (
  output Sign,
  output RegWrite,
  output [5:0] funct
);


  assign funct = 6'b000111;
  assign RegWrite = 1'b1;
  assign Sign = 1'b0;
endmodule

module ori (
  output Sign,
  output RegWrite,
  output [5:0] funct
);


  assign funct = 6'b000110;
  assign RegWrite = 1'b1;
  assign Sign = 1'b0;
endmodule

module bne (
  input  Equal,
  output nbranch,
  output Sign,
  output RegWrite,
  output [1:0] PCSel
);

  Multiplexer #(.width(2), .enable("false")) multiplexer_1 (.in0(2'b01), .in1(2'b00), .out(PCSel), .sel(Equal));

  assign nbranch = 1'b0;
  assign RegWrite = 1'b0;
  assign Sign = 1'b1;
endmodule

module sw (
  output Sign,
  output RegWrite,
  output [5:0] funct,
  output MemWrite
);


  assign funct = {6{1'b0}};
  assign MemWrite = 1'b1;
  assign RegWrite = 1'b0;
  assign Sign = 1'b1;
endmodule

module lui (
  output Sign,
  output RegWrite,
  output [5:0] funct,
  output islui
);


  assign funct = 6'b000010;
  assign islui = 1'b1;
  assign RegWrite = 1'b1;
  assign Sign = 1'b0;
endmodule

module lw (
  output Sign,
  output RegWrite,
  output [5:0] funct,
  output MemRead
);


  assign funct = {6{1'b0}};
  assign MemRead = 1'b1;
  assign RegWrite = 1'b1;
  assign Sign = 1'b1;
endmodule

module disp (
  output Sign,
  output RegWrite
);


  assign RegWrite = 1'b0;
  assign Sign = 1'b0;
endmodule

module jal (
  input  [15:0] CurrentPC,
  input  [15:0] Target_addr,
  output [15:0] jumpaddr,
  output [1:0] PCSel
);

  wire [11:0] target_addr_t;
  wire [15:0] and_1_out, bit_extender_1_out;

  BitSelector #(.width(16), .group(12)) bitselector_1 (.in(Target_addr), .out(target_addr_t), .sel(1'b0));
  assign bit_extender_1_out = {{4{1'b0}}, target_addr_t};  // Bit_Extender bit_extender_1
  assign and_1_out = CurrentPC & 16'hf000;  // AND_Gate and_1, 16 bits wide
  assign jumpaddr = and_1_out | bit_extender_1_out;  // OR_Gate or_1, 16 bits wide

  assign PCSel = 2'b10;
endmodule

module j (
  input  [15:0] CurrentPC,
  input  [15:0] Target_Addr,
  output [15:0] jumpaddr,
  output [1:0] PCSel
);

  wire [11:0] target_addr_t;
  wire [15:0] and_1_out, bit_extender_1_out;

  BitSelector #(.width(16), .group(12)) bitselector_1 (.in(Target_Addr), .out(target_addr_t), .sel(1'b0));
  assign bit_extender_1_out = {{4{1'b0}}, target_addr_t};  // Bit_Extender bit_extender_1
  assign and_1_out = CurrentPC & 16'hf000;  // AND_Gate and_1, 16 bits wide
  assign jumpaddr = and_1_out | bit_extender_1_out;  // OR_Gate or_1, 16 bits wide

  assign PCSel = 2'b10;
endmodule

module jr (
  input  [15:0] in_1,
  output [1:0] rs
);

  BitSelector #(.width(16), .group(2)) bitselector_1 (.in(in_1), .out(rs), .sel(3'b101));
endmodule

module Type_Decoder (
  input  [15:0] in_1,
  output [1:0] Type
);

  wire [3:0] opcode;

  BitSelector #(.width(16), .group(4)) bitselector_1 (.in(in_1), .out(opcode), .sel(2'b11));
  Multiplexer #(.select(4), .width(2), .enable("false")) multiplexer_1 (
    .in0(2'b00), .in1(2'b01), .in2(2'b01), .in3(2'b01), .in4(2'b10), .in5(2'b10), .in6(2'b10), .in7(2'b10),
    .in8(2'b10), .in9(2'b10), .in10(2'b10), .in11(2'b10), .in12(2'b10), .out(Type), .sel(opcode));  // open: in13, in14, in15
endmodule

module ext (
  input  in_1,
  input  [7:0] in_2,
  output [15:0] Result
);

  wire not_1_out;
  wire [15:0] bit_extender_1_out, bit_extender_2_out;

  not not_1 (not_1_out, in_1);
  assign bit_extender_1_out = {{8{1'b0}}, in_2};  // Bit_Extender bit_extender_1
  assign bit_extender_2_out = {{8{in_2[7]}}, in_2};  // Bit_Extender bit_extender_2
  assign Result = not_1_out ? bit_extender_1_out : 16'bz;  // Controlled_Buffer controlled_buffer_1
  assign Result = in_1 ? bit_extender_2_out : 16'bz;  // Controlled_Buffer controlled_buffer_2
endmodule

module ALUsrcSel (
  input  [1:0] in_1,
  output Sign
);

  wire comparator_1_eq, comparator_1_gt, not_1_out, not_2_out, not_3_out;

  Comparator #(.width(2), .mode("unsigned")) comparator_1 (
    .a(in_1), .b(2'b00), .gt(comparator_1_gt), .eq(comparator_1_eq));  // open: lt
  not not_1 (not_1_out, comparator_1_eq);
  assign Sign = not_1_out ? comparator_1_gt : 1'bz;  // Controlled_Buffer controlled_buffer_1
  not not_2 (not_2_out, comparator_1_gt);
  assign Sign = not_2_out ? not_3_out : 1'bz;  // Controlled_Buffer controlled_buffer_2
  not not_3 (not_3_out, comparator_1_eq);
endmodule

module Address_Data_Select (
  input  [15:0] ALUresult,
  input  [15:0] Address,
  input  MemRead,
  input  MemWrite,
  output [15:0] Data_In,
  output [15:0] Address_2
);

  wire not_1_out, or_1_out;

  Multiplexer #(.width(16), .enable("false")) multiplexer_1 (
    .in0(ALUresult), .in1(Address), .out(Data_In), .sel(or_1_out));
  or or_1 (or_1_out, MemRead, MemWrite);
  not not_1 (not_1_out, or_1_out);
  Multiplexer #(.width(16), .enable("false")) multiplexer_2 (
    .in0(ALUresult), .in1(Address), .out(Address_2), .sel(not_1_out));

  // Other names for the same wires on the sheet: Addr[15:0] = Address_2; Data[15:0] = Data_In
endmodule

module luiswitch (
  input  [15:0] _8,
  input  [15:0] imm,
  input  in_3,
  output [15:0] Data_In,
  output [15:0] Address
);

  wire not_1_out;

  Multiplexer #(.width(16), .enable("false")) multiplexer_1 (.in0(_8), .in1(imm), .out(Data_In), .sel(in_3));
  not not_1 (not_1_out, in_3);
  Multiplexer #(.width(16), .enable("false")) multiplexer_2 (.in0(_8), .in1(imm), .out(Address), .sel(not_1_out));

  // Other names for the same wires on the sheet: arg0[15:0] = Data_In; arg1[15:0] = Address; result[15:0] = _8
endmodule

module nPC_sel (
  input  [15:0] CurrInstr,
  input  [15:0] Immediate,
  input  [15:0] JumpAddr,
  input  [1:0] in_4,
  output [15:0] NewPC
);

  wire [15:0] adder_1_out, adder_2_out;

  Adder #(.width(16)) adder_1 (.a(16'h1), .b(CurrInstr), .out(adder_1_out));  // open: cin, cout
  Adder #(.width(16)) adder_2 (.a(CurrInstr), .b(Immediate), .out(adder_2_out));  // open: cin, cout
  Multiplexer #(.select(2), .width(16)) multiplexer_1 (
    .in0(adder_1_out), .in1(adder_2_out), .in2(JumpAddr), .out(NewPC), .sel(in_4));  // open: in3, en
endmodule
